# Fritzing sketch Controller_v3 - trial 6.3.4 mux fix filled (saved by Fritzing 0.9.6b)
circuit board: 14.2cm x 15cm
breadboards: 1

parts:
  LM393-1 = IC, DIP package, 8 pins [chip_label=IC]
  CD4013B-1 = IC, DIP package, 14 pins [chip_label=IC]
  L1 = Inductor [package="400 mil [THT]"]
  Q1 = pnp-Powertransistor [package="TO220 [THT]"]
  555 = IC, DIP package, 8 pins [chip_label=IC]
  C2 = Ceramic Capacitor [capacitance=100nF voltage=35V package="100 mil [THT, multilayer]"]
  R1 = Resistor [tolerance=±5% power=0.25 resistance=220 package=THT]
  R2 = Resistor [tolerance=±5% power=0.25 resistance=220 package=THT]
  L2 = Inductor [package="400 mil [THT]"]
  LM393-2 = IC, DIP package, 8 pins [chip_label=IC]
  CD4013B-2 = IC, DIP package, 14 pins [chip_label=IC]
  L3 = Inductor [package="400 mil [THT]"]
  L4 = Inductor [package="400 mil [THT]"]
  Q3 = pnp-Powertransistor [package="TO220 [THT]"]
  DAC-1 = mystery part, 6 pins [chip_label=MCP4725]
  Fan-1 = mystery part, 4 pins [chip_label="Fan Header"]
  tiny85-1 = attiny85 [package=dip]
  Arduino_Nano = Arduino Nano (Rev3.0)
  I2C_Mux = Adafruit TCA9548A
  FRAM = mystery part, 8 pins [chip_label="32KB FRAM"]
  EEPROM = 24LC256 [package=THT]
  RTC = mystery part, 5 pins [chip_label=PCF8523]
  Mux = IC, DIP package, 16 pins [chip_label=CD4051BE]
  Buzzer = Piezo Speaker
  Q5 = NPN-Transistor [package="TO92 [THT]"]
  R3 = Resistor [tolerance=±5% power=0.25 resistance=220 package=THT]
  R5 = Resistor [tolerance=±5% power=0.25 resistance=220 package=THT]
  R7 = Resistor [tolerance=±5% power=0.25 resistance=220 package=THT]
  R9 = Resistor [tolerance=±5% power=0.25 resistance=220 package=THT]
  R11 = Resistor [tolerance=±5% power=0.25 resistance=220 package=THT]
  R13 = Resistor [tolerance=±5% power=0.25 resistance=220 package=THT]
  DAC-2 = mystery part, 6 pins [chip_label=MCP4725]
  Fan-2 = mystery part, 4 pins [chip_label="Fan Header"]
  DAC-3 = mystery part, 6 pins [chip_label=MCP4725]
  Fan-3 = mystery part, 4 pins [chip_label="Fan Header"]
  DAC-4 = mystery part, 6 pins [chip_label=MCP4725]
  Fan-4 = mystery part, 4 pins [chip_label="Fan Header"]
  IR1 = TSOP312.., 314.. [package=THT]
  LCD = mystery part, 5 pins [chip_label="I2C LCD 16x2"]
  RGB1 = mystery part, 4 pins [chip_label="RGB Header"]
  Q6 = Basic FET N-Channel [package="TO220 [THT]"]
  Q7 = Basic FET N-Channel [package="TO220 [THT]"]
  Q8 = Basic FET N-Channel [package="TO220 [THT]"]
  Q9 = Basic FET N-Channel [package="TO220 [THT]"]
  Q10 = Basic FET N-Channel [package="TO220 [THT]"]
  Q11 = Basic FET N-Channel [package="TO220 [THT]"]
  RGB3 = mystery part, 4 pins [chip_label="RGB Header"]
  Q12 = Basic FET N-Channel [package="TO220 [THT]"]
  Q13 = Basic FET N-Channel [package="TO220 [THT]"]
  Q14 = Basic FET N-Channel [package="TO220 [THT]"]
  RGB4 = mystery part, 4 pins [chip_label="RGB Header"]
  Q15 = PNP-Transistor [package="TO92 [THT]"]
  Q16 = PNP-Transistor [package="TO92 [THT]"]
  R14 = Resistor [tolerance=±5% power=0.25 resistance=10k package=THT]
  R15 = Resistor [tolerance=±5% power=0.25 resistance=4.7k package=THT]
  R16 = Resistor [tolerance=±5% power=0.25 resistance=4.7k package=THT]
  R17 = Resistor [tolerance=±5% power=0.25 resistance=10k package=THT]
  HDD1 = mystery part, 2 pins [chip_label=HDD]
  HDD2 = mystery part, 2 pins [chip_label=HDD]
  R18 = Resistor [tolerance=±5% power=0.25 resistance=10k package=THT]
  LED1 = LED - 5mm [color="Red (633nm)" current=0.030 package="5 mm [THT]"]
  R19 = Resistor [tolerance=±5% power=0.25 resistance=220 package=THT]
  R20 = Resistor [tolerance=±5% power=0.25 resistance=47 package=THT]
  C6 = Ceramic Capacitor [capacitance=100nF voltage=35V package="100 mil [THT, multilayer]"]
  C8 = Ceramic Capacitor [capacitance=100nF voltage=35V package="100 mil [THT, multilayer]"]
  C10 = Ceramic Capacitor [capacitance=100nF voltage=35V package="100 mil [THT, multilayer]"]
  C11 = Ceramic Capacitor [capacitance=100nF voltage=35V package="100 mil [THT, multilayer]"]
  C12 = Ceramic Capacitor [capacitance=100nF voltage=35V package="100 mil [THT, multilayer]"]
  C13 = Ceramic Capacitor [capacitance=100nF voltage=35V package="100 mil [THT, multilayer]"]
  TH4 = mystery part, 2 pins [chip_label=Thermistor]
  TH2 = mystery part, 2 pins [chip_label=Thermistor]
  TH3 = mystery part, 2 pins [chip_label=Thermistor]
  TH1 = mystery part, 2 pins [chip_label=Thermistor]
  Molex = COMPUTER-PERIPHERAL-POWER [package=computer-peripheral-power-ra]
  C14 = Ceramic Capacitor [capacitance=100nF voltage=35V package="100 mil [THT, multilayer]"]
  C15 = Ceramic Capacitor [capacitance=100nF voltage=35V package="100 mil [THT, multilayer]"]
  C16 = Ceramic Capacitor [capacitance=100nF voltage=35V package="100 mil [THT, multilayer]"]
  C17 = Ceramic Capacitor [capacitance=100nF voltage=35V package="100 mil [THT, multilayer]"]
  C18 = Ceramic Capacitor [capacitance=100nF voltage=35V package="100 mil [THT, multilayer]"]
  C19 = Ceramic Capacitor [capacitance=100nF voltage=35V package="100 mil [THT, multilayer]"]
  C21 = Electrolytic Capacitor [capacitance=0.22µF voltage=10V package="100 mil [THT, electrolytic]"]
  Fan-5 = mystery part, 4 pins [chip_label="Fan Header"]
  LDR = mystery part, 2 pins [chip_label=LDR]
  Q2 = pnp-Powertransistor [package="TO220 [THT]"]
  Q4 = pnp-Powertransistor [package="TO220 [THT]"]
  D4 = Rectifier Diode [part_number=1N4001 package="300 mil [THT]"]
  D1 = Rectifier Diode [part_number=1N4001 breakdown_voltage=3.6V package="300 mil [THT]"]
  D2 = Rectifier Diode [part_number=1N4001 breakdown_voltage=3.6V package="300 mil [THT]"]
  D3 = Rectifier Diode [part_number=1N4001 breakdown_voltage=3.6V package="300 mil [THT]"]
  R21 = Resistor [tolerance=±5% power=0.25 resistance=47k package=THT]
  R22 = Resistor [tolerance=±5% power=0.25 resistance=68k package=THT]
  R23 = Resistor [tolerance=±5% power=0.25 resistance=68k package=THT]
  R24 = Resistor [tolerance=±5% power=0.25 resistance=47k package=THT]
  R25 = Resistor [tolerance=±5% power=0.25 resistance=47k package=THT]
  R26 = Resistor [tolerance=±5% power=0.25 resistance=68k package=THT]
  R27 = Resistor [tolerance=±5% power=0.25 resistance=68k package=THT]
  R28 = Resistor [tolerance=±5% power=0.25 resistance=47k package=THT]
  C1 = Electrolytic Capacitor [capacitance=0.22mF voltage=20V package="200 mil [THT, electrolytic]"]
  C3 = Electrolytic Capacitor [capacitance=0.22mF voltage=20V package="200 mil [THT, electrolytic]"]
  C5 = Electrolytic Capacitor [capacitance=0.22mF voltage=20V package="200 mil [THT, electrolytic]"]
  C4 = Electrolytic Capacitor [capacitance=0.22mF voltage=35V package="200 mil [THT, electrolytic]"]
  C20 = Electrolytic Capacitor [capacitance=0.22mF voltage=16V package="200 mil [THT, electrolytic]"]
  PWM_4 = mystery part, 4 pins [chip_label=?]
  PWM_3 = mystery part, 4 pins [chip_label=?]
  PWM_2 = mystery part, 4 pins [chip_label=?]
  PWM_1 = mystery part, 4 pins [chip_label=?]
  PWM_I2C = mystery part, 6 pins [chip_label=?]
  Fan-6 = mystery part, 4 pins [chip_label="Fan Header"]
  C22 = Electrolytic Capacitor [capacitance=0.22µF voltage=10V package="100 mil [THT, electrolytic]"]
  C23 = Ceramic Capacitor [capacitance=100nF voltage=35V package="100 mil [THT, multilayer]"]
  R29 = Resistor [tolerance=±5% power=0.25 resistance=2.2k package=THT]
  R30 = Resistor [tolerance=±5% power=0.25 resistance=2.2k package=THT]
  R31 = Resistor [tolerance=±5% power=0.25 resistance=220 package=THT]
  R32 = Resistor [tolerance=±5% power=0.25 resistance=220 package=THT]
  R33 = Resistor [tolerance=±5% power=0.25 resistance=220 package=THT]
  R34 = Resistor [tolerance=±5% power=0.25 resistance=220 package=THT]
  R35 = Resistor [tolerance=±5% power=0.25 resistance=10k package=THT]
  R36 = Resistor [tolerance=±5% power=0.25 resistance=10k package=THT]
  R37 = Resistor [tolerance=±5% power=0.25 resistance=10k package=THT]
  R38 = Resistor [tolerance=±5% power=0.25 resistance=10k package=THT]
  C24 = Ceramic Capacitor [capacitance=100nF voltage=35V package="100 mil [THT, multilayer]"]
  R39 = Resistor [tolerance=±5% power=0.25 resistance=22k package=THT]
  Reset = mystery part, 2 pins [chip_label=Reset]
  Q17 = NPN-Transistor [package="TO92 [THT]"]
  Q18 = NPN-Transistor [package="TO92 [THT]"]
  Q19 = NPN-Transistor [package="TO92 [THT]"]
  Q20 = NPN-Transistor [package="TO92 [THT]"]
  Q21 = NPN-Transistor [package="TO92 [THT]"]
  Q22 = NPN-Transistor [package="TO92 [THT]"]
  R41 = Resistor [tolerance=±5% power=0.25 resistance=220 package=THT]
  R42 = Resistor [tolerance=±5% power=0.25 resistance=220 package=THT]
  R43 = Resistor [tolerance=±5% power=0.25 resistance=220 package=THT]
  R44 = Resistor [tolerance=±5% power=0.25 resistance=220 package=THT]
  R45 = Resistor [tolerance=±5% power=0.25 resistance=220 package=THT]
  R46 = Resistor [tolerance=±5% power=0.25 resistance=220 package=THT]
  tiny85-2 = attiny85 [package=dip]
  R47 = Resistor [tolerance=±5% power=0.25 resistance=10k package=THT]
  R48 = Resistor [tolerance=±5% power=0.25 resistance=10k package=THT]
  R49 = Resistor [tolerance=±5% power=0.25 resistance=10k package=THT]
  R50 = Resistor [tolerance=±5% power=0.25 resistance=10k package=THT]
  R51 = Resistor [tolerance=±5% power=0.25 resistance=10k package=THT]
  R52 = Resistor [tolerance=±5% power=0.25 resistance=10k package=THT]
  R53 = Resistor [tolerance=±5% power=0.25 resistance=220 package=THT]
  R54 = Resistor [tolerance=±5% power=0.25 resistance=220 package=THT]
  R55 = Resistor [tolerance=±5% power=0.25 resistance=220 package=THT]
  R56 = Resistor [tolerance=±5% power=0.25 resistance=220 package=THT]
  R57 = Resistor [tolerance=±5% power=0.25 resistance=220 package=THT]
  R58 = Resistor [tolerance=±5% power=0.25 resistance=220 package=THT]
  R59 = Resistor [tolerance=±5% power=0.25 resistance=220 package=THT]
  R60 = Resistor [tolerance=±5% power=0.25 resistance=220 package=THT]
  Q23 = NPN-Transistor [package="TO92 [THT]"]
  Q24 = NPN-Transistor [package="TO92 [THT]"]
  Q25 = NPN-Transistor [package="TO92 [THT]"]
  Q26 = NPN-Transistor [package="TO92 [THT]"]
  C25 = Electrolytic Capacitor [capacitance=0.22mF voltage=16V package="200 mil [THT, electrolytic]"]
  R61 = Resistor [tolerance=±5% power=0.25 resistance=10k package=THT]
  RGB2 = mystery part, 4 pins [chip_label="RGB Header"]

nets (from the pcb view):
  N1: LM393-1.pin1, CD4013B-1.pin5, R35.Pin_1
  N2: LM393-1.pin2, DAC-1.pin6
  N3: LM393-1.pin3, R23.Pin_1, R24.Pin_1
  N4: LM393-1.pin4, CD4013B-1.pin4, CD4013B-1.pin6, CD4013B-1.pin7, CD4013B-1.pin8, CD4013B-1.pin10, R24.Pin_0
  N5: LM393-1.pin5, R21.Pin_0, R22.Pin_0
  N6: LM393-1.pin6, DAC-2.pin6
  N7: LM393-1.pin7, CD4013B-1.pin9, R36.Pin_1
  N8: LM393-1.pin8, CD4013B-1.pin14, Q1.emitter, 555.pin4, 555.pin8, C11.1, Q2.emitter, C20.+, R35.Pin_0, R36.Pin_0, C24.1, R61.Pin_0
  N9: CD4013B-1.pin1, R31.Pin_1
  N10: CD4013B-1.pin3, CD4013B-1.pin11, 555.pin3, CD4013B-2.pin3, CD4013B-2.pin11
  N11: CD4013B-1.pin13, R32.Pin_0
  N12: L1.pin_0, Fan-1.pin2, R23.Pin_0, C1.+
  N13: L1.pin_1, Q1.collector, D1.cathode
  N14: Q1.base, R31.Pin_0
  N15: 555.pin1, R1.Pin_1, C11.0, R21.Pin_1, C24.0
  N16: 555.pin2, 555.pin6, R2.Pin_1
  N17: 555.pin5, R1.Pin_0
  N18: 555.pin7, C2.1, R2.Pin_0, R61.Pin_1
  N19: L2.pin_0, Fan-2.pin2, R22.Pin_1, C3.+
  N20: L2.pin_1, Q2.collector, D2.cathode
  N21: LM393-2.pin1, CD4013B-2.pin5, R37.Pin_1
  N22: LM393-2.pin2, DAC-3.pin6
  N23: LM393-2.pin3, R26.Pin_1, R28.Pin_1
  N24: LM393-2.pin4, R28.Pin_0, C25.-
  N25: LM393-2.pin5, R25.Pin_0, R27.Pin_0
  N26: LM393-2.pin6, DAC-4.pin6
  N27: LM393-2.pin7, CD4013B-2.pin9, R38.Pin_1
  N28: LM393-2.pin8, CD4013B-2.pin14, Q3.emitter, C12.1, Q4.emitter, R37.Pin_0, R38.Pin_0, C25.+
  N29: CD4013B-2.pin1, R33.Pin_1
  N30: CD4013B-2.pin4, CD4013B-2.pin6, CD4013B-2.pin7, CD4013B-2.pin8, CD4013B-2.pin10
  N31: CD4013B-2.pin13, R34.Pin_0
  N32: L3.pin_0, Fan-4.pin2, R27.Pin_1, C4.+
  N33: L3.pin_1, Q4.collector, D4.cathode
  N34: L4.pin_0, Fan-3.pin2, R26.Pin_0, C5.+
  N35: L4.pin_1, Q3.collector, D3.cathode
  N36: Q3.base, R33.Pin_0
  5V: DAC-1.pin1, tiny85-1.Pin_8, Arduino_Nano.5V, I2C_Mux.VCC, FRAM.pin1, EEPROM.+V, RTC.pin2, Buzzer.pin1, DAC-2.pin1, DAC-3.pin1, DAC-4.pin1, IR1.Vs, LCD.pin2, RGB3.pin1, Q15.E, Q16.E, R15.Pin_0, R16.Pin_0, C8.1, C10.1, C13.1, TH4.pin1, TH2.pin1, TH3.pin1, TH1.pin1, Molex.5V, C14.1, C15.1, C16.1, C17.1, C18.1, C19.1, C21.+, LDR.pin1, PWM_I2C.pin5, C23.0, R29.Pin_0, R30.Pin_0, tiny85-2.Pin_8
  N37: DAC-1.pin2, DAC-2.pin2, DAC-3.pin2, DAC-4.pin2, C8.0, C10.0
  N38: DAC-1.pin3, I2C_Mux.2SCL
  N39: DAC-1.pin4, I2C_Mux.2SDA
  N40: DAC-1.pin5, DAC-2.pin5, DAC-3.pin5, DAC-4.pin5
  N41: Fan-1.pin3, Mux.pin15, R47.Pin_0
  N42: Fan-1.pin4, Q22.C
  N43: tiny85-1.Pin_1, PWM_3.pin2
  N44: tiny85-1.Pin_2, PWM_3.pin1
  N45: tiny85-1.Pin_3, PWM_4.pin4
  N46: tiny85-1.Pin_5, R41.Pin_0
  N47: tiny85-1.Pin_6, R42.Pin_0
  N48: tiny85-1.Pin_7, R43.Pin_0
  N49: Arduino_Nano.RESET, Reset.pin2
  N50: Arduino_Nano.D2, IR1.Data
  N51: Arduino_Nano.D3, R20.Pin_0, R39.Pin_1
  N52: Arduino_Nano.D4, R3.Pin_0
  N53: Arduino_Nano.D5, R19.Pin_0
  N54: Arduino_Nano.D6, PWM_I2C.pin2
  N55: Arduino_Nano.D7, EEPROM.WP_-_Write_Protect
  N56: Arduino_Nano.D8, FRAM.pin3
  N57: Arduino_Nano.D9, R53.Pin_0
  N58: Arduino_Nano.D10, R54.Pin_0
  N59: Arduino_Nano.D11/MOSI, R55.Pin_0
  N60: Arduino_Nano.D12/MISO, R56.Pin_0
  N61: Arduino_Nano.A7, R5.Pin_1, LDR.pin2
  N62: Arduino_Nano.A6, R13.Pin_0, TH3.pin2
  N63: Arduino_Nano.A5, I2C_Mux.INPUTSCL
  N64: Arduino_Nano.A4, I2C_Mux.INPUTSDA
  N65: Arduino_Nano.A3, I2C_Mux.RESET
  N66: Arduino_Nano.A2, R11.Pin_0, TH1.pin2
  N67: Arduino_Nano.A1, R9.Pin_0, TH4.pin2
  N68: Arduino_Nano.A0, R7.Pin_0, TH2.pin2
  N69: I2C_Mux.3SDA, DAC-2.pin4
  N70: I2C_Mux.3SCL, DAC-2.pin3
  N71: I2C_Mux.4SDA, DAC-3.pin4
  N72: I2C_Mux.4SCL, DAC-3.pin3
  N73: I2C_Mux.5SDA, DAC-4.pin4
  N74: I2C_Mux.5SCL, DAC-4.pin3
  N75: I2C_Mux.6SDA, FRAM.pin5, PWM_I2C.pin4
  N76: I2C_Mux.6SCL, FRAM.pin4, PWM_I2C.pin3
  N77: I2C_Mux.7SDA, RTC.pin3
  N78: I2C_Mux.7SCL, RTC.pin4
  N79: I2C_Mux.GND, C15.0
  N80: I2C_Mux.0SDA, LCD.pin3
  N81: I2C_Mux.0SCL, LCD.pin4
  N82: I2C_Mux.1SDA, EEPROM.SDA_-_I2C_Data, R30.Pin_1
  N83: I2C_Mux.1SCL, EEPROM.SCL_-_I2C_Clock, R29.Pin_1
  N84: FRAM.pin2, FRAM.pin6, FRAM.pin7, FRAM.pin8, R25.Pin_1, PWM_I2C.pin1
  N85: EEPROM.A1, EEPROM.A2
  N86: Mux.pin1, Fan-6.pin3, R51.Pin_0
  N87: Mux.pin2, Mux.pin4
  N88: Mux.pin3, R20.Pin_1
  N89: Mux.pin5, Fan-5.pin3, R52.Pin_0
  N90: Mux.pin6, R60.Pin_0, Q23.C
  N91: Mux.pin7, Mux.pin8
  N92: Mux.pin9, R59.Pin_0, Q24.C
  N93: Mux.pin10, R58.Pin_0, Q25.C
  N94: Mux.pin11, R57.Pin_0, Q26.C
  N95: Mux.pin12, Fan-4.pin3, R50.Pin_0
  N96: Mux.pin13, Fan-3.pin3, R49.Pin_0
  N97: Mux.pin14, Fan-2.pin3, R48.Pin_0
  N98: Mux.pin16, C6.1, Fan-5.pin2, Fan-6.pin2, R47.Pin_1, R48.Pin_1, R49.Pin_1, R50.Pin_1, R51.Pin_1, R52.Pin_1, R57.Pin_1, R58.Pin_1, R59.Pin_1, R60.Pin_1
  N99: Buzzer.pin2, Q5.C
  N100: Q5.B, R3.Pin_1
  N101: R7.Pin_1, R9.Pin_1, R11.Pin_1
  N102: Fan-2.pin4, Q21.C
  N103: Fan-3.pin4, Q20.C
  N104: Fan-4.pin4, Q19.C
  N105: LCD.pin5, PWM_3.pin3
  N106: RGB1.pin1, C22.+, RGB2.pin1
  N107: RGB1.pin2, Q6.drain
  N108: RGB1.pin3, Q7.drain
  N109: RGB1.pin4, Q8.drain
  N110: Q6.gate, PWM_1.pin4
  N111: Q7.gate, PWM_1.pin3
  N112: Q8.gate, PWM_1.pin2
  N113: Q9.gate, PWM_1.pin1
  N114: Q9.drain, RGB2.pin2
  N115: Q9.source, C22.-
  N116: Q10.gate, PWM_2.pin3
  N117: Q10.drain, RGB2.pin4
  N118: Q11.gate, PWM_2.pin4
  N119: Q11.drain, RGB2.pin3
  N120: RGB3.pin2, Q14.drain, RGB4.pin2
  N121: RGB3.pin3, Q12.drain, RGB4.pin3
  N122: RGB3.pin4, Q13.drain, RGB4.pin4
  N123: Q12.gate, PWM_2.pin1
  N124: Q13.gate, PWM_3.pin4
  N125: Q13.source, R18.Pin_0, C21.-
  N126: Q14.gate, PWM_2.pin2
  N127: RGB4.pin1, Q15.C, Q16.C, R18.Pin_1
  N128: Q15.B, R14.Pin_0, R16.Pin_1
  N129: Q16.B, R15.Pin_1, R17.Pin_0
  N130: R14.Pin_1, HDD2.pin1
  N131: R17.Pin_1, HDD1.pin1
  N132: LED1.anode, R19.Pin_1
  N133: C18.0, Q17.E, Q18.E, Q19.E, Q20.E, Q21.E, Q22.E
  N134: Fan-5.pin1, Fan-6.pin1
  N135: Fan-5.pin4, Q18.C
  N136: Q2.base, R32.Pin_1
  N137: Q4.base, R34.Pin_1
  N138: PWM_4.pin1, tiny85-2.Pin_3
  N139: PWM_4.pin2, tiny85-2.Pin_2
  N140: PWM_4.pin3, tiny85-2.Pin_1
  N141: Fan-6.pin4, Q17.C
  N142: Q17.B, R44.Pin_1
  N143: Q18.B, R45.Pin_1
  N144: Q19.B, R46.Pin_1
  N145: Q20.B, R43.Pin_1
  N146: Q21.B, R42.Pin_1
  N147: Q22.B, R41.Pin_1
  N148: R44.Pin_0, tiny85-2.Pin_7
  N149: R45.Pin_0, tiny85-2.Pin_6
  N150: R46.Pin_0, tiny85-2.Pin_5
  N151: R53.Pin_1, Q26.B
  N152: R54.Pin_1, Q25.B
  N153: R55.Pin_1, Q24.B
  N154: R56.Pin_1, Q23.B
  N155: Q25.E, Q26.E

notes:
  Big Chungus was here
  Mr Buzzy
  EMI Zone
  RGB Fan Controller Project v3.1
  Powerrrrrrr
  R1 SHOULD BE A CAPACITOR

custom parts:
  Adafruit TCA9548A: You just found the perfect I2C sensor, and you want to wire up two or three or more of them to your Arduino when you realize "Uh oh, this chip has a fixed I2C address, and from what I know about I2C, you cannot have two devices with the same address on the same SDA/SCL pins!" Are you out of luck? You would be, if you didn't have this ultra-cool TCA9548A 1-to-8 I2C multiplexer! Finally, a way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
